# Fritzing sketch BLECentralSketch (saved by Fritzing 0.9.3b)

parts:
  Part1 = SparkFun ESP8266 Thing
  Part2 = Bluetooth HM-10

nets:
  GND: Part1.GND, Part2.GND
  VCC: Part1.VCC, Part2.VCC
  N1: Part1.GPIO13, Part2.TXD
  N2: Part1.GPIO12, Part2.RXD
